# Fritzing sketch heizung (saved by Fritzing 0.9.3b)
circuit board: 8.46667cm x 5.64444cm
breadboards: 1

parts:
  Raspberry_Pi_1 = Raspberry Pi 3 [part_number=RPI-3-V1.2]
  DS1 = DS18B20 1-Wire Temperature Sensor [part_number=DS18B20]
  R1 = Resistor [tolerance=±5% resistance=220 package=THT]
  R2 = Resistor [tolerance=±5% resistance=220 package=THT]
  R3 = Resistor [tolerance=±5% resistance=220 package=THT]
  R4 = Resistor [tolerance=±5% resistance=220 package=THT]
  R5 = Resistor [tolerance=±5% resistance=220 package=THT]
  R6 = Resistor [tolerance=±5% resistance=220 package=THT]
  R7 = Resistor [tolerance=±5% resistance=220 package=THT]
  R8 = Resistor [tolerance=±5% resistance=220 package=THT]
  R9 = Resistor [tolerance=±5% resistance=220 package=THT]

nets:
  N1: Raspberry_Pi_1.GPIO4, DS1.DQ
  N2: Raspberry_Pi_1.3V3, R1.Pin_1
  N3: Raspberry_Pi_1.GPIO5, R6.Pin_0
  N4: Raspberry_Pi_1.GPIO6, R5.Pin_0
  N5: Raspberry_Pi_1.GPIO13, R4.Pin_0
  N6: Raspberry_Pi_1.GPIO19, R3.Pin_0
  N7: Raspberry_Pi_1.GPIO26, R2.Pin_0
  N8: Raspberry_Pi_1.GPIO21, R9.Pin_0
  N9: Raspberry_Pi_1.GPIO20, R8.Pin_0
  N10: Raspberry_Pi_1.GPIO16, R7.Pin_0
  GND: Raspberry_Pi_1.GND, DS1.GND
  5V: Raspberry_Pi_1.5V, DS1.VDD
  R1: R2.Pin_1
  R2: R3.Pin_1
  R3: R4.Pin_1
  R4: R5.Pin_1
  R5: R6.Pin_1
  R6: R7.Pin_1
  R7: R8.Pin_1
  R8: R9.Pin_1
